// Logisim project divisor.circ as structural Verilog: 1 circuit, main circuit main
module main (
  input  in_1,
  input  in_2,
  input  in_3,
  input  in_4,
  input  Divident___4_Bit,
  input  in_6,
  input  in_7,
  input  in_8,
  output out_9,
  output Quotient___4_Bit,
  output out_11,
  output out_12,
  output out_13,
  output out_14,
  output out_15,
  output out_16
);

  wire adder_1_cout, adder_1_out, adder_2_cout, adder_2_out, adder_3_cout, adder_3_out, adder_4_cout,
       adder_4_out, adder_5_cout, adder_5_out, adder_6_cout, adder_6_out, and_1_out, and_2_out, and_3_out,
       and_4_out, multiplexer_1_out, multiplexer_2_out, multiplexer_3_out, multiplexer_4_out,
       multiplexer_5_out, multiplexer_6_out, multiplexer_7_out, multiplexer_8_out, multiplexer_9_out,
       multiplexer_10_out, not_6_out, not_8_out, not_10_out, not_12_out, or_1_out, or_2_out, or_3_out,
       or_4_out, or_5_out, or_6_out, xor_1_out, xor_2_out, xor_3_out, xor_4_out;

  Adder #(.width(1)) adder_1 (
    .a(in_1), .b(multiplexer_3_out), .out(adder_1_out), .cin(adder_2_cout), .cout(adder_1_cout));
  or or_1 (or_1_out, in_1, adder_3_cout);
  not not_1 (out_13, multiplexer_1_out);
  Multiplexer #(.enable("false")) multiplexer_1 (
    .in0(adder_1_out), .in1(multiplexer_3_out), .out(multiplexer_1_out), .sel(adder_1_cout));
  Adder #(.width(1)) adder_2 (
    .a(in_2), .b(multiplexer_5_out), .out(adder_2_out), .cin(adder_4_cout), .cout(adder_2_cout));
  Adder #(.width(1)) adder_3 (
    .a(in_2), .b(multiplexer_6_out), .out(adder_3_out), .cin(adder_5_cout), .cout(adder_3_cout));
  or or_2 (or_2_out, in_1, in_2);
  or or_3 (or_3_out, in_1, in_2);
  not not_2 (out_14, multiplexer_2_out);
  Multiplexer #(.enable("false")) multiplexer_2 (
    .in0(adder_2_out), .in1(multiplexer_5_out), .out(multiplexer_2_out), .sel(adder_1_cout));
  Multiplexer #(.enable("false")) multiplexer_3 (
    .in0(adder_3_out), .in1(multiplexer_6_out), .out(multiplexer_3_out), .sel(or_1_out));
  or or_4 (or_4_out, or_2_out, adder_6_cout);
  or or_5 (or_5_out, or_3_out, in_3);
  not not_3 (out_15, multiplexer_4_out);
  Multiplexer #(.enable("false")) multiplexer_4 (
    .in0(adder_4_out), .in1(multiplexer_8_out), .out(multiplexer_4_out), .sel(adder_1_cout));
  Adder #(.width(1)) adder_4 (.a(in_3), .b(multiplexer_8_out), .out(adder_4_out), .cin(and_2_out), .cout(adder_4_cout));
  Multiplexer #(.enable("false")) multiplexer_5 (
    .in0(adder_5_out), .in1(multiplexer_9_out), .out(multiplexer_5_out), .sel(or_1_out));
  Adder #(.width(1)) adder_5 (.a(in_3), .b(multiplexer_9_out), .out(adder_5_out), .cin(and_3_out), .cout(adder_5_cout));
  Multiplexer #(.enable("false")) multiplexer_6 (
    .in0(adder_6_out), .in1(multiplexer_10_out), .out(multiplexer_6_out), .sel(or_4_out));
  Adder #(.width(1)) adder_6 (
    .a(in_3), .b(multiplexer_10_out), .out(adder_6_out), .cin(and_1_out), .cout(adder_6_cout));
  or or_6 (or_6_out, or_5_out, and_4_out);
  not not_4 (out_16, multiplexer_7_out);
  Multiplexer #(.enable("false")) multiplexer_7 (
    .in0(xor_1_out), .in1(not_6_out), .out(multiplexer_7_out), .sel(adder_1_cout));
  xor xor_1 (xor_1_out, in_4, not_6_out);
  Multiplexer #(.enable("false")) multiplexer_8 (
    .in0(xor_2_out), .in1(not_8_out), .out(multiplexer_8_out), .sel(or_1_out));
  xor xor_2 (xor_2_out, in_4, not_8_out);
  Multiplexer #(.enable("false")) multiplexer_9 (
    .in0(xor_3_out), .in1(not_10_out), .out(multiplexer_9_out), .sel(or_4_out));
  and and_1 (and_1_out, in_4, not_10_out);
  xor xor_3 (xor_3_out, in_4, not_10_out);
  Multiplexer #(.disabled(0), .enable("false")) multiplexer_10 (
    .in0(xor_4_out), .in1(not_12_out), .out(multiplexer_10_out), .sel(or_6_out));
  xor xor_4 (xor_4_out, in_4, not_12_out);
  and and_2 (and_2_out, in_4, not_6_out);
  and and_3 (and_3_out, in_4, not_8_out);
  and and_4 (and_4_out, in_4, not_12_out);
  not not_5 (out_12, adder_1_cout);
  not not_6 (not_6_out, in_8);
  not not_7 (out_11, or_1_out);
  not not_8 (not_8_out, in_7);
  not not_9 (Quotient___4_Bit, or_4_out);
  not not_10 (not_10_out, in_6);
  not not_11 (out_9, or_6_out);
  not not_12 (not_12_out, Divident___4_Bit);

  // Notes on the sheet:
  //   Remainder - 4 Bit
  //   Divisor- 4 Bit 
endmodule
